# Fritzing sketch step1 (saved by Fritzing 0.9.3b)
breadboards: 1

parts:
  Part1 = Ambient Light Sensor (TEMT6000 Breakout Board)  # not connected
  Part2 = Arduino Uno (Rev3)
  J1 = Infrared Proximity Sensor
  Tiny_RTC2 = Tiny RTC
  Part3 = RFID-RC522-v2
  M1 = Dagu DGServo 9g (Pan and tilt) [part_number=RS001B]

nets:
  N1: Part2.A1, J1.Vout
  N2: Part2.A4/SDA, Tiny_RTC2.SDA
  N3: Part2.A5/SCL, Tiny_RTC2.SCL
  N4: Part2.D9_PWM, M1.pulse
  N5: Part2.D10_PWM/SS, Part3.SDA
  N6: Part2.D11_PWM/MOSI, Part3.MOSI
  N7: Part2.D12/MISO, Part3.MISO
  N8: Part2.D13/SCK, Part3.SCK
  3V3: Part2.3V3, Part3.3.3V
  VCC: Part2.5V, J1.Vcc, Tiny_RTC2.VCC, M1.vcc
  GND: Part2.GND, J1.GND, Tiny_RTC2.GND, Part3.GND, M1.gnd

custom parts:
  Tiny RTC: Tiny RTC I2C module DS1370Z RTC and AT24C32 EEPROM
  RFID-RC522-v2: A simple China made RFID-RC522 Reader; do check the pin labels, as this is a MFRC522 based clone.
